# Fritzing sketch circuit (saved by Fritzing 0.9.10b)
circuit board: 5cm x 8.5cm
breadboards: 1

parts:
  SD = Adafruit MicroSD card breakout board [part_number="Adafruit #254"]
  A2 = Basic Flex Resistor
  BLE = Bluetooth HC-05 Macho
  A0 = Basic Flex Resistor
  2k = Resistor [tolerance=±5% power=0.25 resistance=2k package=THT]
  A1 = Basic Flex Resistor
  IMU = Grove 3 Axis Digital Accelerometer 16g
  Batt = Battery block 9V
  10k = Resistor [tolerance=±5% power=0.25 resistance=10k package=THT]
  A3 = Basic Flex Resistor
  10k_2 = Resistor [tolerance=±5% power=0.25 resistance=10k package=THT]
  10k_3 = Resistor [tolerance=±5% power=0.25 resistance=10k package=THT]
  Nano = Arduino Nano (Rev3.0)
  1k = Resistor [tolerance=±5% power=0.25 resistance=1k package=THT]
  10k_4 = Resistor [tolerance=±5% power=0.25 resistance=10k package=THT]

nets:
  VCC: SD.VCC, BLE.VCC, 10k.Pin_1, 10k_2.Pin_1, 10k_3.Pin_1, Nano.5V, 10k_4.Pin_1
  GND: SD.GND, A2.pin_1, BLE.GND, A0.pin_1, 2k.Pin_0, A1.pin_1, IMU.GND, Batt.-, A3.pin_1, Nano.GND
  N1: SD.CLK, Nano.D13/SCK
  N2: SD.DO, Nano.D12/MISO
  N3: SD.DI, Nano.D11/MOSI
  N4: SD.CS, Nano.D10
  N5: A2.Pin_2, Nano.A2, 10k_4.Pin_0
  N6: BLE.TXD, Nano.D3
  N7: BLE.RXD, 2k.Pin_1, 1k.Pin_1
  N8: A0.Pin_2, 10k_2.Pin_0, Nano.A0
  N9: A1.Pin_2, 10k_3.Pin_0, Nano.A1
  VCC_2: IMU.VCC, Nano.3V3
  N10: IMU.SDA, Nano.A4
  N11: IMU.SCL, Nano.A5
  N12: Batt.+, Nano.VIN
  N13: 10k.Pin_0, A3.Pin_2, Nano.A3
  N14: Nano.D2, 1k.Pin_0

custom parts:
  Adafruit MicroSD card breakout board: Not just a simple breakout board, this microSD adapter goes the extra mile - designed for ease of use. Onboard 5v->3v regulator provides 150mA for power-hungry cards 3v level shifting means you can use this with ease on either 3v or 5v systems Uses a proper level shifting chip, not resistors: less problems, and faster read/write access Use 3 or 4 digital pins to read and write 2Gb+ of storage!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
