# Fritzing sketch circuit (saved by Fritzing 0.9.10b)
circuit board: 5cm x 8.5cm
breadboards: 1

parts:
  A2 = Basic Flex Resistor
  A0 = Basic Flex Resistor
  A1 = Basic Flex Resistor
  IMU = Grove 3 Axis Digital Accelerometer 16g
  10k = Resistor [tolerance=±5% power=0.25 resistance=10k package=THT]
  A3 = Basic Flex Resistor
  10k_2 = Resistor [tolerance=±5% power=0.25 resistance=10k package=THT]
  10k_3 = Resistor [tolerance=±5% power=0.25 resistance=10k package=THT]
  Nano = Arduino Nano (Rev3.0)
  10k_4 = Resistor [tolerance=±5% power=0.25 resistance=10k package=THT]

nets:
  N1: A2.Pin_2, Nano.A2, 10k_4.Pin_0
  GND: A2.pin_1, A0.pin_1, A1.pin_1, IMU.GND, A3.pin_1, Nano.GND
  N2: A0.Pin_2, 10k_2.Pin_0, Nano.A0
  N3: A1.Pin_2, 10k_3.Pin_0, Nano.A1
  VCC: IMU.VCC, Nano.3V3
  N4: IMU.SDA, Nano.A4
  N5: IMU.SCL, Nano.A5
  N6: 10k.Pin_0, A3.Pin_2, Nano.A3
  N7: 10k.Pin_1, 10k_2.Pin_1, 10k_3.Pin_1, Nano.5V, 10k_4.Pin_1
